// Logisim project Add-sub.circ as structural Verilog: 1 circuit, main circuit main
module main (
  input  A2,
  input  A1,
  input  A0,
  input  B2,
  input  B1,
  input  B0,
  input  Control,
  output Sign,
  output Output_3,
  output Output_2,
  output Output_1,
  output Output_0
);

  wire full_adder_1_carry_out, full_adder_2_carry_out, full_adder_3_carry_out, xor_1_out, xor_2_out,
       xor_3_out, xor_4_out;

  xor xor_1 (xor_1_out, B0, Control);
  xor xor_2 (xor_2_out, B1, Control);
  xor xor_3 (xor_3_out, B2, Control);
  xor xor_4 (xor_4_out, B2, Control);
  Full___Adder full_adder_1 (
    .Carry_in(Control), .Inp1(xor_1_out), .Inp2(A0), .Output(Output_0), .Carry_out(full_adder_1_carry_out));
  Full___Adder full_adder_2 (
    .Carry_in(full_adder_1_carry_out), .Inp1(xor_2_out), .Inp2(A1), .Output(Output_1),
    .Carry_out(full_adder_2_carry_out));
  Full___Adder full_adder_3 (
    .Carry_in(full_adder_2_carry_out), .Inp1(xor_3_out), .Inp2(A2), .Output(Output_2),
    .Carry_out(full_adder_3_carry_out));
  Full___Adder full_adder_4 (
    .Carry_in(full_adder_3_carry_out), .Inp1(xor_4_out), .Inp2(A2), .Output(Output_3), .Carry_out(Sign));
endmodule
