// Logisim project Builders.circ as structural Verilog: 5 circuits, main circuit Half - Adder
module Half___Adder (
  input  Inp1,
  input  Inp2,
  output Result,
  output Carry_out
);

  xor xor_1 (Result, Inp1, Inp2);
  and and_1 (Carry_out, Inp1, Inp2);
endmodule

module Full___Adder (
  input  Carry_in,
  input  Inp1,
  input  Inp2,
  output Output,
  output Carry_out
);

  wire and_1_out, and_2_out, or_1_out;

  xor xor_1 (Output, Carry_in, Inp1, Inp2);
  and and_1 (and_1_out, Inp1, Inp2);
  or or_1 (or_1_out, Inp1, Inp2);
  and and_2 (and_2_out, Carry_in, or_1_out);
  or or_2 (Carry_out, and_1_out, and_2_out);
endmodule

module _4Bit_2s__Signed (
  input  Input_Signed,
  input  Input_2,
  input  Input_1,
  input  Input_0,
  output Sign,
  output Output_3,
  output Output_2,
  output Output_1,
  output Output_0
);

  wire half_adder_1_carry_out, half_adder_2_carry_out, xor_1_out, xor_2_out, xor_3_out;

  xor xor_1 (xor_1_out, Input_0, Input_Signed);
  xor xor_2 (xor_2_out, Input_1, Input_Signed);
  xor xor_3 (xor_3_out, Input_2, Input_Signed);
  Half___Adder half_adder_1 (
    .Inp1(Input_Signed), .Inp2(xor_1_out), .Result(Output_0), .Carry_out(half_adder_1_carry_out));
  Half___Adder half_adder_2 (
    .Inp1(half_adder_1_carry_out), .Inp2(xor_2_out), .Result(Output_1), .Carry_out(half_adder_2_carry_out));
  Half___Adder half_adder_3 (.Inp1(half_adder_2_carry_out), .Inp2(xor_3_out), .Result(Output_2), .Carry_out(Output_3));

  assign Sign = Input_Signed;
endmodule

module Binary____BCD (
  input  I4,
  input  I3,
  input  I2,
  input  I1,
  input  I0,
  output TEN,
  output Output_3,
  output Output_2,
  output Output_1,
  output Output_0
);

  wire and_1_out, and_2_out, and_4_out, and_5_out, and_6_out, and_7_out, not_1_out, not_2_out, not_3_out;

  not not_1 (not_1_out, I3);
  not not_2 (not_2_out, I2);
  not not_3 (not_3_out, I1);
  and and_1 (and_1_out, I3, I1);
  and and_2 (and_2_out, I3, I2);
  and and_3 (Output_3, I3, not_2_out, not_3_out);
  and and_4 (and_4_out, not_1_out, I2);
  and and_5 (and_5_out, I2, I1);
  and and_6 (and_6_out, not_1_out, I1);
  and and_7 (and_7_out, I3, I2, not_3_out);
  or or_1 (TEN, I4, and_1_out, and_2_out);
  or or_2 (Output_2, I4, and_4_out, and_5_out);
  or or_3 (Output_1, I4, and_6_out, and_7_out);

  assign Output_0 = I0;
endmodule

module _5Bit_2s__Signed (
  input  Input_Signed,
  input  Input_3,
  input  Input_2,
  input  Input_1,
  input  Input_0,
  output Sign,
  output Output_4,
  output Output_3,
  output Output_2,
  output Output_1,
  output Output_0
);

  wire half_adder_1_carry_out, half_adder_2_carry_out, half_adder_3_carry_out, xor_1_out, xor_2_out,
       xor_3_out, xor_4_out;

  xor xor_1 (xor_1_out, Input_0, Input_Signed);
  xor xor_2 (xor_2_out, Input_1, Input_Signed);
  xor xor_3 (xor_3_out, Input_2, Input_Signed);
  xor xor_4 (xor_4_out, Input_3, Input_Signed);
  Half___Adder half_adder_1 (
    .Inp1(Input_Signed), .Inp2(xor_1_out), .Result(Output_0), .Carry_out(half_adder_1_carry_out));
  Half___Adder half_adder_2 (
    .Inp1(half_adder_1_carry_out), .Inp2(xor_2_out), .Result(Output_1), .Carry_out(half_adder_2_carry_out));
  Half___Adder half_adder_3 (
    .Inp1(half_adder_2_carry_out), .Inp2(xor_3_out), .Result(Output_2), .Carry_out(half_adder_3_carry_out));
  Half___Adder half_adder_4 (.Inp1(half_adder_3_carry_out), .Inp2(xor_4_out), .Result(Output_3), .Carry_out(Output_4));

  assign Sign = Input_Signed;
endmodule
