// Logisim project Full.circ as structural Verilog: 1 circuit, main circuit main
module main (
  input  in_1,
  input  in_2,
  input  in_3,
  input  in_4,
  input  in_5,
  input  in_6,
  input  in_7,
  input  in_8
);

  wire binary_bcd_1_output_0, binary_bcd_1_output_1, binary_bcd_1_output_2, binary_bcd_1_output_3,
       binary_bcd_1_ten, main_1_output_0, main_1_output_1, main_1_output_2, main_1_output_3, main_2_r0,
       main_2_r1, main_2_r2, main_2_r3, main_2_r4, main_2_r5, multiplexer_1_out, n4bit_2s_signed_1_output_0,
       n4bit_2s_signed_1_output_1, n4bit_2s_signed_1_output_2, n4bit_2s_signed_1_output_3,
       n4bit_2s_signed_1_sign, n5bit_2s_signed_1_output_0, n5bit_2s_signed_1_output_1,
       n5bit_2s_signed_1_output_2, n5bit_2s_signed_1_output_3, n5bit_2s_signed_1_output_4,
       n7_segment_display_driver_1_p1, n7_segment_display_driver_1_p3, n7_segment_display_driver_1_p5,
       n7_segment_display_driver_1_p7, n7_segment_display_driver_1_p8, n7_segment_display_driver_1_p9,
       n7_segment_display_driver_1_p10, n7_segment_display_driver_1_p11, n7_segment_display_driver_2_p1,
       n7_segment_display_driver_2_p2, n7_segment_display_driver_2_p3, n7_segment_display_driver_2_p4,
       n7_segment_display_driver_2_p5, n7_segment_display_driver_2_p6, n7_segment_display_driver_2_p7,
       n7_segment_display_driver_2_p8, n7_segment_display_driver_2_p9, n7_segment_display_driver_2_p10,
       n7_segment_display_driver_2_p11;

  Add_sub_main main_1 (
    .A2(in_1), .A1(in_2), .A0(in_3), .B2(in_4), .B1(in_5), .B0(in_6), .Control(in_7),
    .Output_3(main_1_output_3), .Output_2(main_1_output_2), .Output_1(main_1_output_1),
    .Output_0(main_1_output_0));  // open: Sign
  Multiplication_main main_2 (
    .A2(in_1), .A1(in_2), .A0(in_3), .B2(in_4), .B1(in_5), .B0(in_6), .R0(main_2_r0), .R1(main_2_r1),
    .R2(main_2_r2), .R3(main_2_r3), .R4(main_2_r4), .R5(main_2_r5));
  _5Bit_2s__Signed u_5bit_2s_signed_1 (
    .Input_Signed(main_2_r4), .Input_3(main_2_r3), .Input_2(main_2_r2), .Input_1(main_2_r1),
    .Input_0(main_2_r0), .Output_4(n5bit_2s_signed_1_output_4), .Output_3(n5bit_2s_signed_1_output_3),
    .Output_2(n5bit_2s_signed_1_output_2), .Output_1(n5bit_2s_signed_1_output_1),
    .Output_0(n5bit_2s_signed_1_output_0));  // open: Sign
  Multiplexer #(.enable("false")) multiplexer_1 (
    .in0(n4bit_2s_signed_1_sign), .in1(main_2_r5), .out(multiplexer_1_out), .sel(in_8));
  Binary____BCD binary_bcd_1 (
    .TEN(binary_bcd_1_ten), .Output_3(binary_bcd_1_output_3), .Output_2(binary_bcd_1_output_2),
    .Output_1(binary_bcd_1_output_1), .Output_0(binary_bcd_1_output_0), .I4(n5bit_2s_signed_1_output_4),
    .I3(n5bit_2s_signed_1_output_3), .I2(n5bit_2s_signed_1_output_2), .I1(n5bit_2s_signed_1_output_1),
    .I0(n5bit_2s_signed_1_output_0));
  _7_Segment_Display u_7_segment_display_1 (.g(multiplexer_1_out));  // open: f, a, b, e, d, c, dp
  _7_Segment_Display u_7_segment_display_2 (
    .g(n7_segment_display_driver_1_p11), .f(n7_segment_display_driver_1_p10),
    .a(n7_segment_display_driver_1_p1), .b(n7_segment_display_driver_1_p3),
    .e(n7_segment_display_driver_1_p9), .d(n7_segment_display_driver_1_p7), .c(n7_segment_display_driver_1_p5));  // open: dp
  // _7_segment_display_driver 7_segment_display_driver_1: pin names not known; wires that end beside it: n7_segment_display_driver_1_p1, 1'b0, n7_segment_display_driver_1_p3, 1'b0, n7_segment_display_driver_1_p5, 1'b0, n7_segment_display_driver_1_p7, n7_segment_display_driver_1_p8, n7_segment_display_driver_1_p9, n7_segment_display_driver_1_p10, n7_segment_display_driver_1_p11
  Multiplexer #(.enable("false")) multiplexer_2 (
    .in0(1'b0), .in1(binary_bcd_1_ten), .out(n7_segment_display_driver_1_p8), .sel(in_8));
  _7_Segment_Display u_7_segment_display_3 (
    .g(n7_segment_display_driver_2_p11), .f(n7_segment_display_driver_2_p10),
    .a(n7_segment_display_driver_2_p1), .b(n7_segment_display_driver_2_p3),
    .e(n7_segment_display_driver_2_p9), .d(n7_segment_display_driver_2_p7), .c(n7_segment_display_driver_2_p5));  // open: dp
  // _7_segment_display_driver 7_segment_display_driver_2: pin names not known; wires that end beside it: n7_segment_display_driver_2_p1, n7_segment_display_driver_2_p2, n7_segment_display_driver_2_p3, n7_segment_display_driver_2_p4, n7_segment_display_driver_2_p5, n7_segment_display_driver_2_p6, n7_segment_display_driver_2_p7, n7_segment_display_driver_2_p8, n7_segment_display_driver_2_p9, n7_segment_display_driver_2_p10, n7_segment_display_driver_2_p11, in_8
  Multiplexer #(.enable("false")) multiplexer_3 (
    .in0(n4bit_2s_signed_1_output_3), .in1(binary_bcd_1_output_3), .out(n7_segment_display_driver_2_p2),
    .sel(in_8));
  Multiplexer #(.enable("false")) multiplexer_4 (
    .in0(n4bit_2s_signed_1_output_2), .in1(binary_bcd_1_output_2), .out(n7_segment_display_driver_2_p4),
    .sel(in_8));
  _4Bit_2s__Signed u_4bit_2s_signed_1 (
    .Input_Signed(main_1_output_3), .Input_2(main_1_output_2), .Input_1(main_1_output_1),
    .Input_0(main_1_output_0), .Sign(n4bit_2s_signed_1_sign), .Output_3(n4bit_2s_signed_1_output_3),
    .Output_2(n4bit_2s_signed_1_output_2), .Output_1(n4bit_2s_signed_1_output_1),
    .Output_0(n4bit_2s_signed_1_output_0));
  Multiplexer #(.enable("false")) multiplexer_5 (
    .in0(n4bit_2s_signed_1_output_1), .in1(binary_bcd_1_output_1), .out(n7_segment_display_driver_2_p6),
    .sel(in_8));
  Multiplexer #(.enable("false")) multiplexer_6 (
    .in0(n4bit_2s_signed_1_output_0), .in1(binary_bcd_1_output_0), .out(n7_segment_display_driver_2_p8),
    .sel(in_8));
endmodule
