// Logisim project Multiplication.circ as structural Verilog: 6 circuits, main circuit main
module main (
  input  A2,
  input  A1,
  input  A0,
  input  B2,
  input  B1,
  input  B0
);

  wire _2S_____SIGNED_r0, _2S_____SIGNED_r1, _2S_____SIGNED_r2, _2S_____SIGNED_r3, _2S_____SIGNED_s,
       Binary_to_BCD_r0, Binary_to_BCD_r1, Binary_to_BCD_r2, Binary_to_BCD_r3, n3_bits_1_r0, n3_bits_1_r1,
       n3_bits_1_r2, n3_bits_1_r3, n3_bits_1_r5, n7_segment_display_driver_1_p1,
       n7_segment_display_driver_1_p3, n7_segment_display_driver_1_p5, n7_segment_display_driver_1_p7,
       n7_segment_display_driver_1_p8, n7_segment_display_driver_1_p9, n7_segment_display_driver_1_p10,
       n7_segment_display_driver_1_p11, n7_segment_display_driver_2_p1, n7_segment_display_driver_2_p3,
       n7_segment_display_driver_2_p5, n7_segment_display_driver_2_p7, n7_segment_display_driver_2_p9,
       n7_segment_display_driver_2_p10, n7_segment_display_driver_2_p11;

  _3_BITS u_3_bits_1 (
    .R0(n3_bits_1_r0), .R1(n3_bits_1_r1), .R2(n3_bits_1_r2), .R3(n3_bits_1_r3), .R5(n3_bits_1_r5), .A2(A2),
    .A1(A1), .A0(A0), .B2(B2), .B1(B1), .B0(B0));  // open: R4
  _2s_____signed _2S_____SIGNED (
    .C(n3_bits_1_r5), .I3(n3_bits_1_r3), .I2(n3_bits_1_r2), .I1(n3_bits_1_r1), .I0(n3_bits_1_r0),
    .S(_2S_____SIGNED_s), .R3(_2S_____SIGNED_r3), .R2(_2S_____SIGNED_r2), .R1(_2S_____SIGNED_r1),
    .R0(_2S_____SIGNED_r0));
  _7_Segment_Display u_7_segment_display_1 (.g(_2S_____SIGNED_s));  // open: f, a, b, e, d, c, dp
  _7_Segment_Display u_7_segment_display_2 (
    .g(n7_segment_display_driver_1_p11), .f(n7_segment_display_driver_1_p10),
    .a(n7_segment_display_driver_1_p1), .b(n7_segment_display_driver_1_p3),
    .e(n7_segment_display_driver_1_p9), .d(n7_segment_display_driver_1_p7), .c(n7_segment_display_driver_1_p5));  // open: dp
  // _7_segment_display_driver 7_segment_display_driver_1: pin names not known; wires that end beside it: n7_segment_display_driver_1_p1, 1'b0, n7_segment_display_driver_1_p3, 1'b0, n7_segment_display_driver_1_p5, 1'b0, n7_segment_display_driver_1_p7, n7_segment_display_driver_1_p8, n7_segment_display_driver_1_p9, n7_segment_display_driver_1_p10, n7_segment_display_driver_1_p11
  Binary____BCD Binary_to_BCD (
    .I3(_2S_____SIGNED_r3), .I2(_2S_____SIGNED_r2), .I1(_2S_____SIGNED_r1), .I0(_2S_____SIGNED_r0),
    .TEN(n7_segment_display_driver_1_p8), .R3(Binary_to_BCD_r3), .R2(Binary_to_BCD_r2),
    .R1(Binary_to_BCD_r1), .R0(Binary_to_BCD_r0));
  _7_Segment_Display u_7_segment_display_3 (
    .g(n7_segment_display_driver_2_p11), .f(n7_segment_display_driver_2_p10),
    .a(n7_segment_display_driver_2_p1), .b(n7_segment_display_driver_2_p3),
    .e(n7_segment_display_driver_2_p9), .d(n7_segment_display_driver_2_p7), .c(n7_segment_display_driver_2_p5));  // open: dp
  // _7_segment_display_driver 7_segment_display_driver_2: pin names not known; wires that end beside it: n7_segment_display_driver_2_p1, Binary_to_BCD_r3, n7_segment_display_driver_2_p3, Binary_to_BCD_r2, n7_segment_display_driver_2_p5, Binary_to_BCD_r1, n7_segment_display_driver_2_p7, Binary_to_BCD_r0, n7_segment_display_driver_2_p9, n7_segment_display_driver_2_p10, n7_segment_display_driver_2_p11
endmodule

module Binary____BCD (
  input  I3,
  input  I2,
  input  I1,
  input  I0,
  output TEN,
  output R3,
  output R2,
  output R1,
  output R0
);

  wire and_1_out, and_2_out, and_4_out, and_5_out, and_6_out, and_7_out, not_1_out, not_2_out, not_3_out,
       not_4_out, not_5_out;

  and and_1 (and_1_out, I3, I1);
  and and_2 (and_2_out, I3, I2);
  and and_3 (R3, I3, not_1_out, not_2_out);
  not not_1 (not_1_out, I2);
  not not_2 (not_2_out, I1);
  not not_3 (not_3_out, I3);
  and and_4 (and_4_out, not_3_out, I2);
  and and_5 (and_5_out, I2, I1);
  not not_4 (not_4_out, I3);
  and and_6 (and_6_out, not_4_out, I1);
  and and_7 (and_7_out, I3, I2, not_5_out);
  not not_5 (not_5_out, I1);
  or or_1 (TEN, and_1_out, and_2_out);
  or or_2 (R2, and_4_out, and_5_out);
  or or_3 (R1, and_6_out, and_7_out);

  assign R0 = I0;
endmodule

module Half_adder (
  input  Inp1,
  input  Inp2,
  output Result,
  output Carry_out
);

  xor xor_1 (Result, Inp1, Inp2);
  and and_1 (Carry_out, Inp1, Inp2);
endmodule

module Full_adder (
  input  Cin,
  input  Inp1,
  input  Inp2,
  output Output,
  output Carry_out
);

  wire and_1_out, and_2_out, or_1_out;

  xor xor_1 (Output, Cin, Inp1, Inp2);
  and and_1 (and_1_out, Inp1, Inp2);
  or or_1 (or_1_out, Inp1, Inp2);
  and and_2 (and_2_out, Cin, or_1_out);
  or or_2 (Carry_out, and_1_out, and_2_out);
endmodule

module _3_BITS (
  input  A2,
  input  A1,
  input  A0,
  input  B2,
  input  B1,
  input  B0,
  output R0,
  output R1,
  output R2,
  output R3,
  output R4,
  output R5
);

  wire B0A1_out, B0A2_out, B1A0_out, B1A1_out, B1A2_out, B2A0_out, B2A1_out, B2A2_out,
       full_adder_1_carry_out, full_adder_1_output, full_adder_2_carry_out, full_adder_2_output,
       full_adder_3_carry_out, full_adder_4_carry_out, half_adder_1_carry_out, half_adder_2_carry_out;

  and B0A0 (R0, B0, A0);
  and B0A1 (B0A1_out, B0, A1);
  nand B0A2 (B0A2_out, B0, A2);
  and B1A0 (B1A0_out, B1, A0);
  and B1A1 (B1A1_out, B1, A1);
  nand B1A2 (B1A2_out, B1, A2);
  Half_adder half_adder_1 (.Inp1(B1A0_out), .Inp2(B0A1_out), .Result(R1), .Carry_out(half_adder_1_carry_out));
  Full_adder full_adder_1 (
    .Cin(half_adder_1_carry_out), .Inp1(B1A1_out), .Inp2(B0A2_out), .Output(full_adder_1_output),
    .Carry_out(full_adder_1_carry_out));
  Full_adder full_adder_2 (
    .Cin(full_adder_1_carry_out), .Inp1(B1A2_out), .Inp2(1'b1), .Output(full_adder_2_output),
    .Carry_out(full_adder_2_carry_out));
  nand B2A0 (B2A0_out, B2, A0);
  nand B2A1 (B2A1_out, B2, A1);
  and B2A2 (B2A2_out, B2, A2);
  Half_adder half_adder_2 (
    .Inp1(full_adder_1_output), .Inp2(B2A0_out), .Result(R2), .Carry_out(half_adder_2_carry_out));
  Full_adder full_adder_3 (
    .Cin(half_adder_2_carry_out), .Inp1(B2A1_out), .Inp2(full_adder_2_output), .Output(R3),
    .Carry_out(full_adder_3_carry_out));
  Full_adder full_adder_4 (
    .Cin(full_adder_3_carry_out), .Inp1(B2A2_out), .Inp2(full_adder_2_carry_out), .Output(R4),
    .Carry_out(full_adder_4_carry_out));
  Half_adder half_adder_3 (.Inp1(full_adder_4_carry_out), .Inp2(1'b1), .Result(R5));  // open: Carry_out
endmodule

module _2s_____signed (
  input  C,
  input  I3,
  input  I2,
  input  I1,
  input  I0,
  output S,
  output R3,
  output R2,
  output R1,
  output R0
);

  wire and_1_out, and_2_out, and_3_out, and_4_out, and_5_out, and_6_out, and_7_out, and_8_out, and_9_out,
       and_10_out, and_11_out, and_12_out, not_1_out, not_2_out, not_3_out, not_4_out, not_5_out, not_6_out,
       not_7_out, not_8_out, not_9_out, not_10_out, not_11_out, not_12_out, not_13_out, not_14_out,
       not_15_out;

  not not_1 (not_1_out, C);
  not not_2 (not_2_out, I2);
  not not_3 (not_3_out, I1);
  not not_4 (not_4_out, I0);
  not not_5 (not_5_out, I3);
  not not_6 (not_6_out, I3);
  not not_7 (not_7_out, C);
  not not_8 (not_8_out, I1);
  not not_9 (not_9_out, I0);
  not not_10 (not_10_out, I2);
  not not_11 (not_11_out, I2);
  not not_12 (not_12_out, C);
  not not_13 (not_13_out, I0);
  not not_14 (not_14_out, I1);
  not not_15 (not_15_out, I1);
  and and_1 (and_1_out, not_1_out, I3);
  and and_2 (and_2_out, I3, not_2_out, not_3_out, not_4_out);
  and and_3 (and_3_out, C, not_5_out, I1);
  and and_4 (and_4_out, C, not_6_out, I2);
  and and_5 (and_5_out, not_7_out, I2);
  and and_6 (and_6_out, I2, not_8_out, not_9_out);
  and and_7 (and_7_out, C, not_10_out, I1);
  and and_8 (and_8_out, C, I3, not_11_out, I0);
  and and_9 (and_9_out, not_12_out, I1);
  and and_10 (and_10_out, I1, not_13_out);
  and and_11 (and_11_out, C, I2, not_14_out, I0);
  and and_12 (and_12_out, C, I3, not_15_out, I0);
  or or_1 (R3, and_1_out, and_2_out, and_3_out, and_4_out);
  or or_2 (R2, and_5_out, and_6_out, and_7_out, and_8_out);
  or or_3 (R1, and_9_out, and_10_out, and_11_out, and_12_out);

  assign R0 = I0;
  assign S = C;
endmodule
